# Fritzing sketch schematic (saved by Fritzing 0.9.3b)
breadboards: 1

parts:
  Part1 = Arduino Nano (Rev3.0)
  VCC = 4 x AAA Battery Mount
  HC-06 = Bluetooth HC-05 Macho
  U1 = L9110 H-bridge [part_number="L9110 H-bridge"]
  Left = DC Motor
  Left_2 = DC Motor
  Right = DC Motor
  Right_2 = DC Motor
  C2 = Electrolytic Capacitor [capacitance=220µF package="200 mil [THT, electrolytic]"]

nets:
  N1: Part1.D1/TX, HC-06.TXD
  N2: Part1.D0/RX, HC-06.RXD
  GND: Part1.GND, VCC.-, HC-06.GND, U1.connector2, C2.-
  N3: Part1.D2, U1.connector4
  N4: Part1.D3, U1.connector5
  N5: Part1.D4, U1.connector0
  N6: Part1.D5, U1.connector1
  5V: Part1.5V, VCC.+, HC-06.VCC, U1.connector3, C2.+
  N7: U1.connector6, Left.pin_2, Left_2.pin_2
  N8: U1.connector7, Left.pin_1, Left_2.pin_1
  N9: U1.connector8, Right.pin_2, Right_2.pin_2
  N10: U1.connector9, Right.pin_1, Right_2.pin_1
